# Fritzing sketch photon+DHT22+photoresistance (saved by Fritzing 0.9.3b)
breadboards: 1

parts:
  Composant1 = Photon
  R2 = Resistor [tolerance=±5% resistance=220 package=THT]
  DHT1 = DHT22 Humidity and Temperature Sensor  # not connected
  R3 = Photocell (LDR) [package=THT]
  Grove1 = Grove OLED 128x96

nets:
  N1: Composant1.A0, R2.Pin_0, R3.pin_1
  GND: Composant1.GND, R2.Pin_1, Grove1.GND
  N2: Composant1.D0, Grove1.SDA
  N3: Composant1.D1, Grove1.SCL
  3V3: Composant1.3V3, R3.pin_0, Grove1.VCC

notes:
  GND
  VCC
  DAT
