# Fritzing sketch photon+leds_rgb_adressables (saved by Fritzing 0.9.3b)
breadboards: 1

parts:
  Composant1 = Photon
  R2 = Resistor [tolerance=±5% resistance=10k package=THT]
  NEOPIXEL1 = Neopixel Strip -- White (60/m) [part_number=1138]
  S2 = Pushbutton [package="[THT]"]
  S3 = Pushbutton [package="[THT]"]
  R3 = Resistor [tolerance=±5% resistance=10k package=THT]

nets:
  GND: Composant1.GND, R2.Pin_1, NEOPIXEL1.GND, R3.Pin_1
  VIN: Composant1.VIN, NEOPIXEL1.+5V
  N1: Composant1.D0, R2.Pin_0, S2.Pin_3, S2.Pin_4
  N2: Composant1.D1, S3.Pin_3, S3.Pin_4, R3.Pin_0
  N3: Composant1.D2, NEOPIXEL1.DI
  N4: Composant1.3V3, S2.Pin_1, S2.Pin_2, S3.Pin_1, S3.Pin_2

custom parts:
  Neopixel Strip -- White (60/m): Neopixel Strip, White, 60 pixels per meter.
