# Fritzing sketch photon+relais_grove+bouton (saved by Fritzing 0.9.3b)
breadboards: 1

parts:
  Grove_Relay1 = Grove Relay
  Composant1 = Photon
  S1 = Pushbutton [package="[THT]"]
  R1 = Resistor [tolerance=±5% resistance=10k package=THT]

nets:
  N1: Grove_Relay1.SIG, Composant1.D4
  VCC: Grove_Relay1.VCC, Composant1.3V3, S1.Pin_1, S1.Pin_2
  GND: Grove_Relay1.GND, Composant1.GND, R1.Pin_1
  N2: Composant1.D0, S1.Pin_3, S1.Pin_4, R1.Pin_0

custom parts:
  Grove Relay: Relay, Grove connector.
