# Fritzing sketch photon+servo (saved by Fritzing 0.9.3b)
breadboards: 1

parts:
  Composant1 = Photon
  S1 = Pushbutton [package="[THT]"]
  S2 = Pushbutton [package="[THT]"]
  R2 = Resistor [tolerance=±5% resistance=10k package=THT]
  R3 = Resistor [tolerance=±5% resistance=10k package=THT]
  J1 = Basic Servo

nets:
  GND: Composant1.GND, R2.Pin_1, R3.Pin_1, J1.gnd
  VIN: Composant1.VIN, J1.vcc
  N1: Composant1.D0, J1.pulse
  N2: Composant1.D3, S1.Pin_3, S1.Pin_4, R3.Pin_0
  N3: Composant1.D4, S2.Pin_3, S2.Pin_4, R2.Pin_0
  N4: Composant1.3V3, S1.Pin_1, S1.Pin_2, S2.Pin_1, S2.Pin_2
